# Fritzing sketch conexiones (saved by Fritzing 0.9.6b)

parts:
  Mod1 = Raspberry Pi Pico W
  Capacitive_Soil_Moisture_Sensor1 = DFRobot Capacitive Soil Moisture Sensor V1.0 [part_number=SEN0193]
  A1 = DHT22 module
  OLED_I2C1 = OLED 128x64 I2C Monochrome Display
  Part1 = BH1750  # not connected
  Mod2 = MQ-135 breakout
  BAT1 = 18650 battery holder [package=battery-18650-kit]  # not connected

nets:
  N1: Mod1.pin_11, OLED_I2C1.SDA
  N2: Mod1.pin_12, OLED_I2C1.SCK
  N3: Mod1.pin_31, Capacitive_Soil_Moisture_Sensor1.A
  N4: Mod1.pin_32, Mod2.AO
  N5: Mod1.pin_33, Mod1.pin_38, Capacitive_Soil_Moisture_Sensor1.GND
  N6: Capacitive_Soil_Moisture_Sensor1.VCC, A1.+

notes:
  Sensor de Humedad de Suelo
  GND
  3.7 V
  GPIO 26
  ANALOG OUTPUT
  GPIO 3
  DIGITAL OUTPUT
  GPIO 8
  GPIO 9
  I2C (SDA)
  I2C (SCL)
  BH1750
  pantalla oled (128x64)
  Sensor de Humedad y Temperatura
  DHT22
  Sensor de Intensidad de Luz
  GPIO 27
  ANALOG
  OUTPUT
  MQ-135
  Sensor de Calidad del aire
  Batería Li-ion 9800 mAh

custom parts:
  Raspberry Pi Pico W: Raspberry Pi Pico W. Based around the RP2040 microcontroller the Pico W is a low cost microcontroller device bringing Raspberry Pi quality, cost, and easy of use to the microcontroller space. The areas marked KEEPOUT in pcb silkscreen should not have traces running through them to avoid shorts on a soldered in module!
  DFRobot Capacitive Soil Moisture Sensor V1.0: DFRobot Capacitive Soil Moisture Sensor V1.0 This product measures soil moisture levels by capacitive sensing, rather than resistive sensing like other types of moisture sensor. It is made of a corrosion resistant material giving it a long service life. Insert it into soil and impress your friends with the real-time soil moisture data! The product includes an on-board voltage regulator which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
  DHT22 module: DHT22 module. Pins VCC Data GND.
  BH1750: Light Sensor
  MQ-135 breakout: MQ-135 gas sensor
  18650 battery holder: 18650 Battery
